# Fritzing sketch rpi-neocam (saved by Fritzing 0.9.0b)
breadboards: 1

parts:
  S1 = Momentary Switch [package=ksa_sealed_tac_switch]
  R1 = Resistor [package="2010 [SMD]"]
  J1 = Cobbler Plus

nets:
  N1: S1.2, R1.Pin_1, J1.EEC
  N2: S1.4, J1.SCLK
  N3: J1.3V3, J1.5.0V

custom parts:
  Cobbler Plus: The Cobbler Plus is an add on prototyping board from Adafruit specifically designed for the Raspberry Pi B+ that can break out all those tasty power, GPIO, I2C and SPI pins from the 40-pin header onto a solderless breadboard. This set will make "cobbling together" prototypes with the Pi super easy. The Cobbler Plus can plug into any solderless breadboard.
